# Fritzing sketch overall (saved by Fritzing 1.0.4)

parts:
  Q1 = Basic FET P-Channel [package="TO220 [THT]"]
  BAT1 = BC9VPC [package=bc9vpc]
  S1 = Toggle Switch [package=THT]
  Mod1 = Raspberry Pi Pico
  M1 = motor driver shz-mdbl-010 [package=THT]
  M2 = DC Motor [voltage_(max)=6V voltage_(min)=3V]
  M3 = DC Motor [voltage_(max)=6V voltage_(min)=3V]
  LED1 = RGB LED (com. anode, rbg) [color="Red (633nm)" current=0.030A package="5 mm [THT]"]

nets:
  N1: Q1.gate, S1.COM
  N2: Q1.drain, BAT1.V-, Mod1.pin_3, Mod1.pin_18, Mod1.pin_38, Mod1.pin_42, M1.pin_6, LED1.common_anode
  N3: Q1.source, Mod1.pin_39, M1.pin_5
  N4: BAT1.V+, S1.L1
  N5: Mod1.pin_15, LED1.green_cathode
  N6: Mod1.pin_16, LED1.blue_cathode
  N7: Mod1.pin_19, LED1.red_cathode
  N8: Mod1.pin_21, M1.pin_10
  N9: Mod1.pin_22, M1.pin_9
  N10: Mod1.pin_24, M1.pin_8
  N11: Mod1.pin_25, M1.pin_7
  N12: M1.pin_1, M3.pin_1
  N13: M1.pin_2, M3.pin_2
  N14: M1.pin_3, M2.pin_2
  N15: M1.pin_4, M2.pin_1

notes:
  Power Switch
  Motor Controller (H Bridge)
  Voltage
  Regulator
  DC Motor
  RGB LED

custom parts:
  Raspberry Pi Pico: Raspberry Pi Pico. Based around the RP2040 microcontroller the Pico is a low cost microcontroller device bringing Raspberry Pi quality, cost, and easy of use to the microcontroller space. Jan 2021, Split part in to two versions: tht (this one) and SMD. This one will drill holes for a .1 in header in pcb to allow plugging in the module as well as providing pads to solder the module to the top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
  motor driver shz-mdbl-010: Motor drive module is ideal for use in battery-powered smart car, toy cars, robots. Supply voltage 2V ~ 10V, can drive two DC motors or a 4-wire 2-phase stepper motors ,can achieve forward rotation or reverse rotation, it is possible to adjust the rotation speed. Each can provide continuous current of 1.5A, peak current up to 2.5A, thermal protection and can be automatically restored.
